// Logisim project proj.circ as structural Verilog: 7 circuits, main circuit main
module main (
);

  wire button_1_out, left, right, up;
  wire [31:0] map_1_out_6, map_1_out_7, map_1_out_8, map_1_out_9, map_1_out_10, map_1_out_11, map_1_out_12,
       map_1_out_13, map_1_out_14, map_1_out_15, map_1_out_16, map_1_out_17, map_1_out_18, map_1_out_19,
       map_1_out_20, map_1_out_21, map_1_out_22, map_1_out_23, map_1_out_24, map_1_out_25, map_1_out_26,
       map_1_out_27, map_1_out_28, map_1_out_29, map_1_out_30, map_1_out_31, map_1_out_32, map_1_out_33,
       map_1_out_34, map_1_out_35, map_1_out_36, map_1_out_37;

  Clock clock_1 ();  // open: out
  Button button_1 (.out(button_1_out));
  DotMatrix #(.inputtype("row"), .matrixcols(32), .matrixrows(32)) dotmatrix_1 (
    .row0(map_1_out_6), .row1(map_1_out_7), .row2(map_1_out_8), .row3(map_1_out_9), .row4(map_1_out_10),
    .row5(map_1_out_11), .row6(map_1_out_12), .row7(map_1_out_13), .row8(map_1_out_14), .row9(map_1_out_15),
    .row10(map_1_out_16), .row11(map_1_out_17), .row12(map_1_out_18), .row13(map_1_out_19),
    .row14(map_1_out_20), .row15(map_1_out_21), .row16(map_1_out_22), .row17(map_1_out_23),
    .row18(map_1_out_24), .row19(map_1_out_25), .row20(map_1_out_26), .row21(map_1_out_27),
    .row22(map_1_out_28), .row23(map_1_out_29), .row24(map_1_out_30), .row25(map_1_out_31),
    .row26(map_1_out_32), .row27(map_1_out_33), .row28(map_1_out_34), .row29(map_1_out_35),
    .row30(map_1_out_36), .row31(map_1_out_37));
  map map_1 (
    .in_2(up), .in_4(left), .in_5(right), .in_3(32'h18000), .out_6(map_1_out_6), .out_7(map_1_out_7),
    .out_8(map_1_out_8), .out_9(map_1_out_9), .out_10(map_1_out_10), .out_11(map_1_out_11),
    .out_12(map_1_out_12), .out_13(map_1_out_13), .out_14(map_1_out_14), .out_15(map_1_out_15),
    .out_16(map_1_out_16), .out_17(map_1_out_17), .out_18(map_1_out_18), .out_19(map_1_out_19),
    .out_20(map_1_out_20), .out_21(map_1_out_21), .out_22(map_1_out_22), .out_23(map_1_out_23),
    .out_24(map_1_out_24), .out_25(map_1_out_25), .out_26(map_1_out_26), .out_27(map_1_out_27),
    .out_28(map_1_out_28), .out_29(map_1_out_29), .out_30(map_1_out_30), .out_31(map_1_out_31),
    .out_32(map_1_out_32), .out_33(map_1_out_33), .out_34(map_1_out_34), .out_35(map_1_out_35),
    .out_36(map_1_out_36), .out_37(map_1_out_37));  // open: shift
  Button button_2 (.out(up));
  Button button_3 (.out(right));
  Button button_4 (.out(left));
endmodule

module map (
  input  shift,
  input  in_2,
  input  [31:0] in_3,
  input  in_4,
  input  in_5,
  output [31:0] out_6,
  output [31:0] out_7,
  output [31:0] out_8,
  output [31:0] out_9,
  output [31:0] out_10,
  output [31:0] out_11,
  output [31:0] out_12,
  output [31:0] out_13,
  output [31:0] out_14,
  output [31:0] out_15,
  output [31:0] out_16,
  output [31:0] out_17,
  output [31:0] out_18,
  output [31:0] out_19,
  output [31:0] out_20,
  output [31:0] out_21,
  output [31:0] out_22,
  output [31:0] out_23,
  output [31:0] out_24,
  output [31:0] out_25,
  output [31:0] out_26,
  output [31:0] out_27,
  output [31:0] out_28,
  output [31:0] out_29,
  output [31:0] out_30,
  output [31:0] out_31,
  output [31:0] out_32,
  output [31:0] out_33,
  output [31:0] out_34,
  output [31:0] out_35,
  output [31:0] out_36,
  output [31:0] out_37
);

  wire clock_1_out, \end , Jump, multiplexer_1_out;
  wire [4:0] counter_1_q, counter_2_q, counter_3_q, counter_4_q, rowPos;
  wire [31:0] char, row0, row1, row2, row3, row4, row5, row6, row7, row8, row9, row10, row11, row12, row13,
       row14, row15, row16, row17, row18, row19, row20, row21, row22, row23, row24, row25, row26, row27,
       row28, row29, row30, row31, shifter_1_out, str0, str1, str2, str3, str4, str5, str6, str7, str8, str9,
       str10, str11, str12, str13, str14, str15, str16, str17, str18, str19, str20, str21, str22, str23,
       str24, str25, str26, str27, str28, str29, str30, str31;

  Clock clock_1 (.out(clock_1_out));
  Multiplexer #(.enable("false")) multiplexer_1 (.in0(clock_1_out), .in1(1'b0), .out(multiplexer_1_out), .sel(Jump));
  Counter #(.width(5), .max('h1f)) counter_1 (.Q(counter_1_q), .clk(in_4));  // open: load, D, count, carry, clr
  Counter #(.width(5), .max('h1f)) counter_2 (.Q(counter_2_q), .clk(in_5));  // open: load, D, count, carry, clr
  Counter #(.width(5), .max('h1f)) counter_3 (.Q(counter_3_q), .clk(in_2));  // open: load, D, count, carry, clr
  Subtractor #(.width(5)) subtractor_1 (.a(counter_3_q), .b(counter_4_q), .out(rowPos));  // open: bin, bout
  Counter #(.width(5), .max('h1f), .trigger("falling")) counter_4 (
    .Q(counter_4_q), .clk(multiplexer_1_out));  // open: load, D, count, carry, clr
  Shifter #(.width(32), .shift("rl")) shifter_1 (.in(in_3), .\dist (counter_1_q), .out(shifter_1_out));
  Demultiplexer #(.select(5), .width(32), .enable("false")) demultiplexer_1 (
    .out0(row0), .out1(row1), .out2(row2), .out3(row3), .out4(row4), .out5(row5), .out6(row6), .out7(row7),
    .out8(row8), .out9(row9), .out10(row10), .out11(row11), .out12(row12), .out13(row13), .out14(row14),
    .out15(row15), .out16(row16), .out17(row17), .out18(row18), .out19(row19), .out20(row20), .out21(row21),
    .out22(row22), .out23(row23), .out24(row24), .out25(row25), .out26(row26), .out27(row27), .out28(row28),
    .out29(row29), .out30(row30), .out31(row31), .in(char), .sel(rowPos));
  Comparator #(.width(5)) comparator_1 (.a(rowPos), .b({5{1'b1}}), .eq(\end ));  // open: gt, lt
  Shifter #(.width(32), .shift("rr")) shifter_2 (.in(shifter_1_out), .\dist (counter_2_q), .out(char));
  isJump isjump_1 (
    .\end (\end ), .shift(shift), .char(char), .rowPos(rowPos), .isJump(Jump), .out_6(str0), .out_7(str1),
    .out_8(str2), .out_9(str3), .out_10(str4), .out_11(str5), .out_12(str6), .out_13(str7), .out_14(str8),
    .out_15(str9), .out_16(str10), .out_17(str11), .out_18(str12), .out_19(str13), .out_20(str14),
    .out_21(str15), .out_22(str16), .out_23(str17), .out_24(str18), .out_25(str19), .out_26(str20),
    .out_27(str21), .out_28(str22), .out_29(str23), .out_30(str24), .out_31(str25), .out_32(str26),
    .out_33(str27), .out_34(str28), .out_35(str29), .out_36(str30), .out_37(str31));
  assign out_6 = str31 | row31;  // OR_Gate or_1, 32 bits wide
  assign out_7 = str30 | row30;  // OR_Gate or_2, 32 bits wide
  assign out_8 = str29 | row29;  // OR_Gate or_3, 32 bits wide
  assign out_9 = str28 | row28;  // OR_Gate or_4, 32 bits wide
  assign out_10 = str27 | row27;  // OR_Gate or_5, 32 bits wide
  assign out_11 = str26 | row26;  // OR_Gate or_6, 32 bits wide
  assign out_12 = str25 | row25;  // OR_Gate or_7, 32 bits wide
  assign out_13 = str24 | row24;  // OR_Gate or_8, 32 bits wide
  assign out_14 = str23 | row23;  // OR_Gate or_9, 32 bits wide
  assign out_15 = str22 | row22;  // OR_Gate or_10, 32 bits wide
  assign out_16 = str21 | row21;  // OR_Gate or_11, 32 bits wide
  assign out_17 = str20 | row20;  // OR_Gate or_12, 32 bits wide
  assign out_18 = str19 | row19;  // OR_Gate or_13, 32 bits wide
  assign out_19 = str18 | row18;  // OR_Gate or_14, 32 bits wide
  assign out_20 = str17 | row17;  // OR_Gate or_15, 32 bits wide
  assign out_21 = str16 | row16;  // OR_Gate or_16, 32 bits wide
  assign out_22 = str15 | row15;  // OR_Gate or_17, 32 bits wide
  assign out_23 = str14 | row14;  // OR_Gate or_18, 32 bits wide
  assign out_24 = str13 | row13;  // OR_Gate or_19, 32 bits wide
  assign out_25 = str12 | row12;  // OR_Gate or_20, 32 bits wide
  assign out_26 = str11 | row11;  // OR_Gate or_21, 32 bits wide
  assign out_27 = str10 | row10;  // OR_Gate or_22, 32 bits wide
  assign out_28 = str9 | row9;  // OR_Gate or_23, 32 bits wide
  assign out_29 = str8 | row8;  // OR_Gate or_24, 32 bits wide
  assign out_30 = str7 | row7;  // OR_Gate or_25, 32 bits wide
  assign out_31 = str6 | row6;  // OR_Gate or_26, 32 bits wide
  assign out_32 = str5 | row5;  // OR_Gate or_27, 32 bits wide
  assign out_33 = str4 | row4;  // OR_Gate or_28, 32 bits wide
  assign out_34 = str3 | row3;  // OR_Gate or_29, 32 bits wide
  assign out_35 = str2 | row2;  // OR_Gate or_30, 32 bits wide
  assign out_36 = str1 | row1;  // OR_Gate or_31, 32 bits wide
  assign out_37 = str0 | row0;  // OR_Gate or_32, 32 bits wide
endmodule

module isW (
  output out_1
);

  wire comparator_1_eq, comparator_2_eq;
  wire [6:0] keyboard_1_data;

  Keyboard keyboard_1 (.clk(1'b1), .data(keyboard_1_data));  // open: re, clr, avail
  Comparator #(.width(7)) comparator_1 (.a(7'b1010111), .b(keyboard_1_data), .eq(comparator_1_eq));  // open: gt, lt
  Comparator #(.width(7)) comparator_2 (.a(keyboard_1_data), .b(7'b1110111), .eq(comparator_2_eq));  // open: gt, lt
  or or_1 (out_1, comparator_1_eq, comparator_2_eq);
endmodule

module checkCollision (
  input  [4:0] rowPos,
  input  [31:0] char,
  input  [31:0] str0,
  input  [31:0] str1,
  input  [31:0] str2,
  input  [31:0] str3,
  input  [31:0] str4,
  input  [31:0] str5,
  input  [31:0] str6,
  input  [31:0] str7,
  input  [31:0] str8,
  input  [31:0] str9,
  input  [31:0] str10,
  input  [31:0] str11,
  input  [31:0] str12,
  input  [31:0] str13,
  input  [31:0] str14,
  input  [31:0] str15,
  input  [31:0] str16,
  input  [31:0] str17,
  input  [31:0] str18,
  input  [31:0] str19,
  input  [31:0] str20,
  input  [31:0] str21,
  input  [31:0] str22,
  input  [31:0] str23,
  input  [31:0] str24,
  input  [31:0] str25,
  input  [31:0] str26,
  input  [31:0] str27,
  input  [31:0] str28,
  input  [31:0] str29,
  input  [31:0] str30,
  input  [31:0] str31,
  output out
);

  wire [7:0] bit_extender_2_out, incdec_1_out;
  wire [31:0] and_1_out, multiplexer_1_out, multiplexer_2_out, multiplexer_3_out, or_1_out;

  Bit_Extender #(.out_width(5)) bit_extender_1 (.in(incdec_1_out));  // open: out
  Bit_Extender #(.in_width(5), .out_width(8)) bit_extender_2 (.out(bit_extender_2_out));  // open: in
  incdec incdec_1 (.in(bit_extender_2_out), .out(incdec_1_out), .up_down(1'b0));
  Multiplexer #(.select(5), .width(32), .disabled(0), .enable("false")) multiplexer_1 (
    .in1(str31), .in2(str30), .in3(str29), .in4(str28), .in5(str27), .in6(str26), .in7(str25), .in8(str24),
    .in9(str23), .in10(str22), .in11(str21), .in12(str20), .in13(str19), .in14(str18), .in15(str17),
    .in16(str16), .in17(str15), .in18(str14), .in19(str13), .in20(str12), .in21(str11), .in22(str10),
    .in23(str9), .in24(str8), .in25(str7), .in26(str6), .in27(str5), .in28(str4), .in29(str3), .in30(str2),
    .in31(str1), .out(multiplexer_1_out), .sel(rowPos));  // open: in0
  Multiplexer #(.select(5), .width(32), .disabled(0), .enable("false")) multiplexer_2 (
    .in0(str31), .in1(str30), .in2(str29), .in3(str28), .in4(str27), .in5(str26), .in6(str25), .in7(str24),
    .in8(str23), .in9(str22), .in10(str21), .in11(str20), .in12(str19), .in13(str18), .in14(str17),
    .in15(str16), .in16(str15), .in17(str14), .in18(str13), .in19(str12), .in20(str11), .in21(str10),
    .in22(str9), .in23(str8), .in24(str7), .in25(str6), .in26(str5), .in27(str4), .in28(str3), .in29(str2),
    .in30(str1), .out(multiplexer_2_out), .sel(rowPos));  // open: in31
  Multiplexer #(.select(5), .width(32), .disabled(0), .enable("false")) multiplexer_3 (
    .in2(str31), .in3(str30), .in4(str29), .in5(str28), .in6(str27), .in7(str26), .in8(str25), .in9(str24),
    .in10(str23), .in11(str22), .in12(str21), .in13(str20), .in14(str19), .in15(str18), .in16(str17),
    .in17(str16), .in18(str15), .in19(str14), .in20(str13), .in21(str12), .in22(str11), .in23(str10),
    .in24(str9), .in25(str8), .in26(str7), .in27(str6), .in28(str5), .in29(str4), .in30(str3), .in31(str2),
    .out(multiplexer_3_out), .sel(rowPos));  // open: in0, in1
  assign or_1_out = multiplexer_3_out | multiplexer_2_out | multiplexer_1_out;  // OR_Gate or_1, 32 bits wide
  assign and_1_out = or_1_out & char;  // AND_Gate and_1, 32 bits wide
  or or_2 (out, and_1_out[0], and_1_out[1], and_1_out[2], and_1_out[3], and_1_out[4], and_1_out[5], and_1_out[6], and_1_out[7], and_1_out[8], and_1_out[9], and_1_out[10], and_1_out[11], and_1_out[12], and_1_out[13], and_1_out[14], and_1_out[15], and_1_out[16], and_1_out[17], and_1_out[18], and_1_out[19], and_1_out[20], and_1_out[21], and_1_out[22], and_1_out[23], and_1_out[24], and_1_out[25], and_1_out[26], and_1_out[27], and_1_out[28], and_1_out[29], and_1_out[30], and_1_out[31]);

  // Other names for the same wires on the sheet: str0_t[31:0] = str31; str1_t[31:0] = str30; str2_t[31:0] = str29;
  //   str3_t[31:0] = str28; str4_t[31:0] = str27; str5_t[31:0] = str26; str6_t[31:0] = str25; str7_t[31:0] = str24;
  //   str8_t[31:0] = str23; str9_t[31:0] = str22; str10_t[31:0] = str21; str11_t[31:0] = str20; str12_t[31:0] = str19;
  //   str13_t[31:0] = str18; str14_t[31:0] = str17; str15_t[31:0] = str16; str16_t[31:0] = str15;
  //   str17_t[31:0] = str14; str18_t[31:0] = str13; str19_t[31:0] = str12; str20_t[31:0] = str11;
  //   str21_t[31:0] = str10; str22_t[31:0] = str9; str23_t[31:0] = str8; str24_t[31:0] = str7; str25_t[31:0] = str6;
  //   str26_t[31:0] = str5; str27_t[31:0] = str4; str28_t[31:0] = str3; str29_t[31:0] = str2; str30_t[31:0] = str1;
  //   str31_t[31:0] = str0
endmodule

// OR
module _5BitOr (
  input  [4:0] num,
  output out
);

  or or_1 (out, num[0], num[1], num[2], num[3], num[4]);
endmodule

// JUMP
module isJump (
  input  \end ,
  input  shift,
  input  [31:0] char,
  input  [4:0] rowPos,
  output isJump,
  output [31:0] out_6,
  output [31:0] out_7,
  output [31:0] out_8,
  output [31:0] out_9,
  output [31:0] out_10,
  output [31:0] out_11,
  output [31:0] out_12,
  output [31:0] out_13,
  output [31:0] out_14,
  output [31:0] out_15,
  output [31:0] out_16,
  output [31:0] out_17,
  output [31:0] out_18,
  output [31:0] out_19,
  output [31:0] out_20,
  output [31:0] out_21,
  output [31:0] out_22,
  output [31:0] out_23,
  output [31:0] out_24,
  output [31:0] out_25,
  output [31:0] out_26,
  output [31:0] out_27,
  output [31:0] out_28,
  output [31:0] out_29,
  output [31:0] out_30,
  output [31:0] out_31,
  output [31:0] out_32,
  output [31:0] out_33,
  output [31:0] out_34,
  output [31:0] out_35,
  output [31:0] out_36,
  output [31:0] out_37
);

  wire and_1_out, checkcollision_1_out, clock_1_out, clock_2_out, comparator_1_gt, controlled_buffer_1_out,
       or_1_out, or_2_out, xor_1_out;
  wire [1:0] counter_1_q;
  wire [4:0] multiplexer_2_out, random_1_out, register_1_q, subtractor_1_out;
  wire [31:0] multiplexer_1_out, shifter_1_out, startgamefield_1_out_1, startgamefield_1_out_2,
       startgamefield_1_out_3, startgamefield_1_out_4, startgamefield_1_out_5, startgamefield_1_out_6,
       startgamefield_1_out_7, startgamefield_1_out_8, startgamefield_1_out_9, startgamefield_1_out_10,
       startgamefield_1_out_11, startgamefield_1_out_12, startgamefield_1_out_13, startgamefield_1_out_14,
       startgamefield_1_out_15, startgamefield_1_out_16, startgamefield_1_out_17, startgamefield_1_out_18,
       startgamefield_1_out_19, startgamefield_1_out_20, startgamefield_1_out_21, startgamefield_1_out_22,
       startgamefield_1_out_23, startgamefield_1_out_24, startgamefield_1_out_25, startgamefield_1_out_26,
       startgamefield_1_out_27, startgamefield_1_out_28, startgamefield_1_out_29, startgamefield_1_out_30,
       startgamefield_1_out_31, startgamefield_1_out_32;

  Clock clock_1 (.out(clock_1_out));
  Random #(.width(5)) random_1 (.clk(controlled_buffer_1_out), .out(random_1_out));  // open: next, clr
  or or_1 (or_1_out, shift, isJump);
  Shifter #(.width(32)) shifter_1 (.in(32'hf), .\dist (random_1_out), .out(shifter_1_out));
  Counter #(.width(2), .max('h3)) counter_1 (
    .Q(counter_1_q), .clk(controlled_buffer_1_out));  // open: load, D, count, carry, clr
  assign controlled_buffer_1_out = or_2_out ? clock_1_out : 1'bz;  // Controlled_Buffer controlled_buffer_1
  or or_2 (or_2_out, or_1_out, \end );
  _5BitOr u_5bitor_1 (.num(subtractor_1_out), .out(isJump));
  Multiplexer #(.select(2), .width(32), .enable("false")) multiplexer_1 (
    .in0(shifter_1_out), .in1(shifter_1_out), .in2(shifter_1_out), .in3(shifter_1_out),
    .out(multiplexer_1_out), .sel(counter_1_q));
  xor xor_1 (xor_1_out, and_1_out, checkcollision_1_out);
  and and_1 (and_1_out, isJump, checkcollision_1_out);
  Shift_Register #(.width(32), .length(32)) shiftRegister (
    .shift(1'b1), .in(multiplexer_1_out), .clk(controlled_buffer_1_out), .load(\end ),
    .d0(startgamefield_1_out_32), .q0(out_37), .d1(startgamefield_1_out_31), .q1(out_36),
    .d2(startgamefield_1_out_30), .q2(out_35), .d3(startgamefield_1_out_29), .q3(out_34),
    .d4(startgamefield_1_out_28), .q4(out_33), .d5(startgamefield_1_out_27), .q5(out_32),
    .d6(startgamefield_1_out_26), .q6(out_31), .d7(startgamefield_1_out_25), .q7(out_30),
    .d8(startgamefield_1_out_24), .q8(out_29), .d9(startgamefield_1_out_23), .q9(out_28),
    .d10(startgamefield_1_out_22), .q10(out_27), .d11(startgamefield_1_out_21), .q11(out_26),
    .d12(startgamefield_1_out_20), .q12(out_25), .d13(startgamefield_1_out_19), .q13(out_24),
    .d14(startgamefield_1_out_18), .q14(out_23), .d15(startgamefield_1_out_17), .q15(out_22),
    .d16(startgamefield_1_out_16), .q16(out_21), .d17(startgamefield_1_out_15), .q17(out_20),
    .d18(startgamefield_1_out_14), .q18(out_19), .d19(startgamefield_1_out_13), .q19(out_18),
    .d20(startgamefield_1_out_12), .q20(out_17), .d21(startgamefield_1_out_11), .q21(out_16),
    .d22(startgamefield_1_out_10), .q22(out_15), .d23(startgamefield_1_out_9), .q23(out_14),
    .d24(startgamefield_1_out_8), .q24(out_13), .d25(startgamefield_1_out_7), .q25(out_12),
    .d26(startgamefield_1_out_6), .q26(out_11), .d27(startgamefield_1_out_5), .q27(out_10),
    .d28(startgamefield_1_out_4), .q28(out_9), .d29(startgamefield_1_out_3), .q29(out_8),
    .d30(startgamefield_1_out_2), .q30(out_7), .d31(startgamefield_1_out_1), .q31(out_6));  // open: out, clr
  Multiplexer #(.width(5), .enable("false")) multiplexer_2 (
    .in0(subtractor_1_out), .in1(5'b01001), .out(multiplexer_2_out), .sel(xor_1_out));
  Register #(.width(5)) register_1 (.D(multiplexer_2_out), .Q(register_1_q), .clk(clock_2_out));  // open: en, clr
  Clock clock_2 (.out(clock_2_out));
  Subtractor #(.width(5)) subtractor_1 (
    .a(register_1_q), .b({5{1'b0}}), .out(subtractor_1_out), .bin(comparator_1_gt));  // open: bout
  checkCollision checkcollision_1 (
    .str0(out_37), .str1(out_36), .str2(out_35), .str3(out_34), .str4(out_33), .str5(out_32), .str6(out_31),
    .str7(out_30), .str8(out_29), .str9(out_28), .str10(out_27), .str11(out_26), .str12(out_25),
    .str13(out_24), .str14(out_23), .str15(out_22), .str16(out_21), .str17(out_20), .str18(out_19),
    .str19(out_18), .str20(out_17), .str21(out_16), .str22(out_15), .str23(out_14), .str24(out_13),
    .str25(out_12), .str26(out_11), .str27(out_10), .str28(out_9), .str29(out_8), .str30(out_7),
    .str31(out_6), .rowPos(rowPos), .char(char), .out(checkcollision_1_out));
  Comparator #(.width(5)) comparator_1 (.a(register_1_q), .b({5{1'b0}}), .gt(comparator_1_gt));  // open: eq, lt
  startGameField startgamefield_1 (
    .out_1(startgamefield_1_out_1), .out_2(startgamefield_1_out_2), .out_3(startgamefield_1_out_3),
    .out_4(startgamefield_1_out_4), .out_5(startgamefield_1_out_5), .out_6(startgamefield_1_out_6),
    .out_7(startgamefield_1_out_7), .out_8(startgamefield_1_out_8), .out_9(startgamefield_1_out_9),
    .out_10(startgamefield_1_out_10), .out_11(startgamefield_1_out_11), .out_12(startgamefield_1_out_12),
    .out_13(startgamefield_1_out_13), .out_14(startgamefield_1_out_14), .out_15(startgamefield_1_out_15),
    .out_16(startgamefield_1_out_16), .out_17(startgamefield_1_out_17), .out_18(startgamefield_1_out_18),
    .out_19(startgamefield_1_out_19), .out_20(startgamefield_1_out_20), .out_21(startgamefield_1_out_21),
    .out_22(startgamefield_1_out_22), .out_23(startgamefield_1_out_23), .out_24(startgamefield_1_out_24),
    .out_25(startgamefield_1_out_25), .out_26(startgamefield_1_out_26), .out_27(startgamefield_1_out_27),
    .out_28(startgamefield_1_out_28), .out_29(startgamefield_1_out_29), .out_30(startgamefield_1_out_30),
    .out_31(startgamefield_1_out_31), .out_32(startgamefield_1_out_32));

  // Other names for the same wires on the sheet: Jump = isJump; str0[31:0] = out_37; str1[31:0] = out_36;
  //   str2[31:0] = out_35; str3[31:0] = out_34; str4[31:0] = out_33; str5[31:0] = out_32; str6[31:0] = out_31;
  //   str7[31:0] = out_30; str8[31:0] = out_29; str9[31:0] = out_28; str10[31:0] = out_27; str11[31:0] = out_26;
  //   str12[31:0] = out_25; str13[31:0] = out_24; str14[31:0] = out_23; str15[31:0] = out_22; str16[31:0] = out_21;
  //   str17[31:0] = out_20; str18[31:0] = out_19; str19[31:0] = out_18; str20[31:0] = out_17; str21[31:0] = out_16;
  //   str22[31:0] = out_15; str23[31:0] = out_14; str24[31:0] = out_13; str25[31:0] = out_12; str26[31:0] = out_11;
  //   str27[31:0] = out_10; str28[31:0] = out_9; str29[31:0] = out_8; str30[31:0] = out_7; str31[31:0] = out_6
endmodule

module startGameField (
  output [31:0] out_1,
  output [31:0] out_2,
  output [31:0] out_3,
  output [31:0] out_4,
  output [31:0] out_5,
  output [31:0] out_6,
  output [31:0] out_7,
  output [31:0] out_8,
  output [31:0] out_9,
  output [31:0] out_10,
  output [31:0] out_11,
  output [31:0] out_12,
  output [31:0] out_13,
  output [31:0] out_14,
  output [31:0] out_15,
  output [31:0] out_16,
  output [31:0] out_17,
  output [31:0] out_18,
  output [31:0] out_19,
  output [31:0] out_20,
  output [31:0] out_21,
  output [31:0] out_22,
  output [31:0] out_23,
  output [31:0] out_24,
  output [31:0] out_25,
  output [31:0] out_26,
  output [31:0] out_27,
  output [31:0] out_28,
  output [31:0] out_29,
  output [31:0] out_30,
  output [31:0] out_31,
  output [31:0] out_32
);


  assign out_1 = {32{1'b0}};
  assign out_2 = {32{1'b0}};
  assign out_3 = 32'he00000;
  assign out_4 = {32{1'b0}};
  assign out_5 = {32{1'b0}};
  assign out_6 = {32{1'b0}};
  assign out_7 = 32'he00000;
  assign out_8 = {32{1'b0}};
  assign out_9 = {32{1'b0}};
  assign out_10 = {32{1'b0}};
  assign out_11 = 32'he00000;
  assign out_12 = {32{1'b0}};
  assign out_13 = {32{1'b0}};
  assign out_14 = {32{1'b0}};
  assign out_15 = 32'he00000;
  assign out_16 = {32{1'b0}};
  assign out_17 = {32{1'b0}};
  assign out_18 = {32{1'b0}};
  assign out_19 = 32'he00000;
  assign out_20 = {32{1'b0}};
  assign out_21 = {32{1'b0}};
  assign out_22 = {32{1'b0}};
  assign out_23 = 32'he00000;
  assign out_24 = {32{1'b0}};
  assign out_25 = {32{1'b0}};
  assign out_26 = {32{1'b0}};
  assign out_27 = 32'he00000;
  assign out_28 = {32{1'b0}};
  assign out_29 = {32{1'b0}};
  assign out_30 = {32{1'b0}};
  assign out_31 = 32'he00000;
  assign out_32 = {32{1'b0}};
endmodule
